# Fritzing sketch VarispeedStepperCircuit (saved by Fritzing 0.9.3b)
breadboards: 1

parts:
  S1 = Toggle Switch [package=THT]
  R1 = Rotary Potentiometer (Small) [maximum_resistance=100kΩ package=THT]
  M1 = Stepper Motor - Bipolar
  Part1 = Arduino Uno (Rev3)
  R2 = Rotary Potentiometer (Small) [maximum_resistance=100kΩ package=THT]
  U1 = LCD-16X2 [package=lcd-16x2]
  PART2 = Big Easy Driver ROB-11876 [part_number=ROB-11876]
  S2 = Momentary Switch [package=ksa_sealed_tac_switch]

nets:
  N1: S1.L1, S1.COM, Part1.D2
  GND: S1.L2, R1.leg1, Part1.GND, R2.leg1, U1.VSS, U1.R_W, U1.K, PART2.GND#30, S2.2
  N2: R1.wiper, U1.VO
  5V: R1.leg2, Part1.5V, R2.leg2, U1.VDD, U1.A
  N3: M1.A, PART2.A#0
  N4: M1.C, PART2.A#1
  N5: M1.B, PART2.B#2
  N6: M1.D, PART2.B#3
  N7: Part1.A0, R2.wiper
  N8: Part1.D8, U1.DB7
  N9: Part1.D9_PWM, PART2.EN
  N10: Part1.D10_PWM/SS, S2.4
  N11: Part1.D11_PWM/MOSI, U1.E
  N12: Part1.D12/MISO, U1.RS
  N13: Part1.D3_PWM, PART2.DR
  N14: Part1.D4, PART2.ST
  N15: Part1.D5_PWM, U1.DB4
  N16: Part1.D6_PWM, U1.DB5
  N17: Part1.D7, U1.DB6

notes:
  5V and Ground
  12V and Ground

custom parts:
  Big Easy Driver ROB-11876: The Big Easy Driver, designed by Brian Schmalz, is a stepper motor driver board for bi-polar stepper motors up to 1.4A/phase. It is based on the Allegro A4988 stepper driver chip. It’s the next version of the popular Easy Driver board. Each Big Easy Driver can drive up to about 1.4A per phase of a bi-polar stepper motor. It is a chopper microstepping driver which defaults to 16 step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
